# Fritzing sketch SensorUltrasonicoLedRgb (saved by Fritzing 0.8.7b)
breadboards: 1

parts:
  Part1 = Arduino Mega ADK (Rev3)
  LED1 = RGB LED (com. anode, rbg) [package="5 mm [THT]"]
  U3 = HC-SR04 [chip_label=IC package="SIP (Single Inline) [THT]"]
  R1 = Resistor [tolerance=±5% resistance=330 package="0603 [SMD]"]
  R2 = Resistor [tolerance=±5% resistance=330 package="0603 [SMD]"]
  R3 = Resistor [tolerance=±5% resistance=330 package="0603 [SMD]"]

nets:
  N1: Part1.D13_PWM, U3.Trig
  N2: Part1.D10_PWM, U3.Echo
  5V: Part1.5V, U3.Vcc
  GND: Part1.GND, LED1.blue_cathode, U3.GND
  N3: Part1.D1/TX0, R1.Pin_0
  N4: Part1.D3_PWM, R2.Pin_0, R3.Pin_0
  N5: LED1.red_cathode, R1.Pin_1
  N6: LED1.common_anode, R2.Pin_1
  N7: LED1.green_cathode, R3.Pin_1

custom parts:
  HC-SR04: HC-SR04 ultrasound distance sensor
